# Fritzing sketch boil_buddy (saved by Fritzing 0.9.3b)
breadboards: 1

parts:
  PIEZO = Crystal [frequency="16 Mhz" package=THT]
  JP1 = USB_MICROB_PLUG [package=micro-b-ra-th]
  R1 = Resistor [tolerance=±5% resistance=10 package=THT]
  R2 = Resistor [tolerance=±5% resistance=3.3M package=THT]
  PocketBeagle = PocketBeagle

nets:
  N1: PIEZO.pin_0, PocketBeagle.AIN.VREFP
  N2: PIEZO.pin_1, R1.Pin_0
  N3: JP1.VCC, PocketBeagle.USB1.VBUS, PocketBeagle.USB1.VIN
  N4: JP1.D-, PocketBeagle.USB1.DN
  N5: JP1.D+, PocketBeagle.USB1.DP
  N6: JP1.ID, PocketBeagle.USB1.ID
  GND: JP1.GND, PocketBeagle.GND
  N7: R1.Pin_1, R2.Pin_0, PocketBeagle.AIN0(1.8V)
  N8: R2.Pin_1, PocketBeagle.AIN.VREFN
